# Fritzing sketch horgaszcucc_panel (saved by Fritzing 0.9.6b)
circuit board: 8.46667cm x 5.64444cm
breadboards: 1

parts:
  A2 = ESP32-S3 supermini
  S1 = Pushbutton [package="[THT]"]
  S2 = Pushbutton [package="[THT]"]
  Part1 = HX711 Weighing Sensor Module
  Squix1 = OLED_SSD1306_I2C_GND_VCC_128x32
  R1 = Resistor [tolerance=±5% power=0.25 resistance=220 package=THT]
  R2 = Resistor [tolerance=±5% power=0.25 resistance=220 package=THT]
  Load_Cell1 = Load Cell - Red/white/black/green  # not connected
  J1 = female pin header, 4 pins [form="♀ (female)"]  # not connected

nets (from the schematic view):
  GND: A2.Pin_1, A2.Pin_39, S1.Pin_1, S1.Pin_2, S2.Pin_1, S2.Pin_2, Part1.GND, Squix1.connector1
  N1: A2.Pin_5, Squix1.connector4
  N2: A2.Pin_6, Squix1.connector3
  N3: A2.Pin_7, Part1.DO/RX
  N4: A2.Pin_8, Part1.CK/TX
  N5: A2.Pin_9, S2.Pin_3, S2.Pin_4, R2.Pin_1
  N6: A2.Pin_10, S1.Pin_3, S1.Pin_4, R1.Pin_1
  5V: A2.Pin_40, Part1.VCC, Squix1.connector2, R1.Pin_0, R2.Pin_0

custom parts:
  ESP32-S3 supermini: Esp32-S3 Development board ESP32 SuperMini development board ESP32 Development board WiFi Bluetooth.
  HX711 Weighing Sensor Module: HX711 is a precision 24-bit analog-to-digital converter (ADC) designed for weigh scales and industrial control applications to interface directly with a bridge sensor.
  Load Cell - Red/white/black/green: A rectangle load cell/weighting pressure Sensor with four wires - Red, white, black, green. Normally corresponding with E+, E-, A+, A- respectively.
